# Fritzing sketch Schematic (saved by Fritzing 1.0.5)
circuit board: 14.0438cm x 6.83193cm

parts:
  Part1 = Arduino Uno (Rev3)
  NEOPIXEL_24 = 24 NeoPixel Ring [part_number=1586]
  RTC = RTC_DS1302
  J1 = female pin header, 3 pins [form="♀ (female)"]

nets:
  N1: Part1.D9_PWM, RTC.RST
  N2: Part1.D10_PWM/SS, RTC.DAT
  N3: Part1.D11_PWM/MOSI, RTC.CLK
  N4: Part1.D6_PWM, NEOPIXEL_24.IN, J1.pin1
  5V: Part1.5V, NEOPIXEL_24.VDD, RTC.VCC, J1.pin2
  GND: Part1.GND, NEOPIXEL_24.GND, RTC.GND, J1.pin3

notes:
  - + IN

custom parts:
  24 NeoPixel Ring: 24 ultra bright smart LED NeoPixels are arranged in a circle with 2.6" (66mm) outer diameter. The rings are 'chainable' - connect the output pin of one to the input pin of another. Use only one microcontroller pin to control as many as you can chain together! Each LED is addressable as the driver chip is inside the LED. Each one has ~18mA constant current drive so the color will be very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
  RTC_DS1302: Arduino module DS1302 SPI Real Time Clock
