# Fritzing sketch Schematic (saved by Fritzing 1.0.5)
circuit board: 10.0127cm x 5.634cm

parts:
  Part1 = Arduino Uno (Rev3)
  RTC = RTC_DS1302
  7_Segment = 7 Segment Display

nets:
  N1: Part1.D8, 7_Segment.Segment_E
  N2: Part1.D9_PWM, RTC.RST
  N3: Part1.D10_PWM/SS, RTC.DAT
  N4: Part1.D11_PWM/MOSI, RTC.CLK
  N5: Part1.D2, 7_Segment.Segment_B
  N6: Part1.D3_PWM, 7_Segment.Segment_A
  N7: Part1.D4, 7_Segment.Segment_G
  N8: Part1.D5_PWM, 7_Segment.Segment_F
  N9: Part1.D6_PWM, 7_Segment.common_cathode#12
  N10: Part1.D7, 7_Segment.Segment_D
  5V: Part1.5V, RTC.VCC
  GND: Part1.GND, RTC.GND, 7_Segment.common_cathode#5, 7_Segment.common_cathode#16

notes:
  ╔═ 3 ═╗
  ║ ║
  5 2
  ║ ║
  ╠═ 4 ═╣
  ║ ║
  8 6
  ║ ║
  ╚═ 7 ═╝

custom parts:
  RTC_DS1302: Arduino module DS1302 SPI Real Time Clock
